// Logisim project logisim_cpu.circ as structural Verilog: 8 circuits, main circuit main
module main (
  input  Clear,
  input  Clear_2
);

  wire im_1_memwrite;
  wire [1:0] im_1_selector;
  wire [2:0] im_1_r_hedef, im_1_r_kaynak1, im_1_r_kaynak2;
  wire [15:0] alu_1_output, mem_1_output, pc_1_output, registers_1_readdata1, registers_1_readdata2;

  PC pc_1 (.CLEAR(Clear_2), .OUTPUT(pc_1_output));
  IM im_1 (
    .INPUT(pc_1_output), .R_Hedef(im_1_r_hedef), .R_Kaynak2(im_1_r_kaynak2), .R_Kaynak1(im_1_r_kaynak1),
    .Selector(im_1_selector), .MemWrite(im_1_memwrite));
  REGISTERS registers_1 (
    .WriteData(mem_1_output), .WriteReg(im_1_r_hedef), .ReadReg1(im_1_r_kaynak1), .ReadReg2(im_1_r_kaynak2),
    .ReadData1(registers_1_readdata1), .ReadData2(registers_1_readdata2));
  ALU alu_1 (
    .INPUT1(registers_1_readdata1), .INPUT2(registers_1_readdata2), .SELECTOR(im_1_selector),
    .OUTPUT(alu_1_output));  // open: OVERFLOW
  MEM mem_1 (
    .ADDRESS(alu_1_output), .Write_Data(registers_1_readdata2), .MemWrite(im_1_memwrite), .Clear(Clear),
    .OUTPUT(mem_1_output));  // open: MemRead
endmodule

module PC (
  input  CLEAR,
  output [15:0] OUTPUT
);

  wire CLOCK_out;
  wire [15:0] adder_1_out;

  Register #(.width(16)) PC (.D(adder_1_out), .en(1'b1), .Q(OUTPUT), .clk(CLOCK_out), .clr(CLEAR));
  Clock CLOCK (.out(CLOCK_out));
  Adder #(.width(16)) adder_1 (.a(16'h1), .b(OUTPUT), .out(adder_1_out));  // open: cin, cout
endmodule

module IM (
  input  [15:0] INPUT,
  output [2:0] R_Hedef,
  output [2:0] R_Kaynak2,
  output [2:0] R_Kaynak1,
  output [1:0] Selector,
  output MemWrite
);

  wire [15:12] rom_1_data;

  ROM #(.addrWidth(16), .dataWidth(16)) rom_1 (
    .addr(INPUT), .data({rom_1_data, MemWrite, Selector, R_Kaynak1, R_Kaynak2, R_Hedef}), .sel(1'b1));
endmodule

// REGS
module REGISTERS (
  input  [2:0] ReadReg1,
  input  [2:0] WriteReg,
  input  [15:0] WriteData,
  input  [2:0] ReadReg2,
  output [15:0] ReadData1,
  output [15:0] ReadData2
);

  wire CLOCK_out, decoder_1_out0, decoder_1_out1, decoder_1_out2, decoder_1_out3, decoder_1_out4,
       decoder_1_out5, decoder_1_out6, decoder_1_out7;
  wire [15:0] register_1_q, register_2_q, register_3_q, register_4_q, register_5_q, register_6_q,
       register_7_q, register_8_q;

  Decoder #(.select(3), .enable("false")) decoder_1 (
    .out0(decoder_1_out0), .out1(decoder_1_out1), .out2(decoder_1_out2), .out3(decoder_1_out3),
    .out4(decoder_1_out4), .out5(decoder_1_out5), .out6(decoder_1_out6), .out7(decoder_1_out7), .sel(WriteReg));
  Register #(.width(16)) register_1 (
    .D(WriteData), .en(decoder_1_out0), .Q(register_1_q), .clk(CLOCK_out));  // open: clr
  Register #(.width(16)) register_2 (
    .D(WriteData), .en(decoder_1_out1), .Q(register_2_q), .clk(CLOCK_out));  // open: clr
  Register #(.width(16)) register_3 (
    .D(WriteData), .en(decoder_1_out2), .Q(register_3_q), .clk(CLOCK_out));  // open: clr
  Register #(.width(16)) register_4 (
    .D(WriteData), .en(decoder_1_out3), .Q(register_4_q), .clk(CLOCK_out));  // open: clr
  Register #(.width(16)) register_5 (
    .D(WriteData), .en(decoder_1_out4), .Q(register_5_q), .clk(CLOCK_out));  // open: clr
  Register #(.width(16)) register_6 (
    .D(WriteData), .en(decoder_1_out5), .Q(register_6_q), .clk(CLOCK_out));  // open: clr
  Register #(.width(16)) register_7 (
    .D(WriteData), .en(decoder_1_out6), .Q(register_7_q), .clk(CLOCK_out));  // open: clr
  Register #(.width(16)) register_8 (
    .D(WriteData), .en(decoder_1_out7), .Q(register_8_q), .clk(CLOCK_out));  // open: clr
  Clock CLOCK (.out(CLOCK_out));
  Multiplexer #(.select(3), .width(16)) multiplexer_1 (
    .in0(register_1_q), .in1(register_2_q), .in2(register_3_q), .in3(register_4_q), .in4(register_5_q),
    .in5(register_6_q), .in6(register_7_q), .in7(register_8_q), .out(ReadData1), .sel(ReadReg1));  // open: en
  Multiplexer #(.select(3), .width(16)) multiplexer_2 (
    .in0(register_1_q), .in1(register_2_q), .in2(register_3_q), .in3(register_4_q), .in4(register_5_q),
    .in5(register_6_q), .in6(register_7_q), .in7(register_8_q), .out(ReadData2), .sel(ReadReg2));  // open: en
endmodule

module ADD_SUB (
  input  [15:0] INPUT1,
  input  SUB,
  input  [15:0] INPUT2,
  output OVERFLOW,
  output [15:0] out_5
);

  wire adder_1_cout, adder_2_cout, adder_3_cout, adder_4_cout, adder_5_cout, adder_6_cout, adder_7_cout,
       adder_8_cout, adder_9_cout, adder_10_cout, adder_11_cout, adder_12_cout, adder_13_cout, adder_14_cout,
       adder_15_cout, adder_16_cout, xor_2_out, xor_3_out, xor_4_out, xor_5_out, xor_6_out, xor_7_out,
       xor_8_out, xor_9_out, xor_10_out, xor_11_out, xor_12_out, xor_13_out, xor_14_out, xor_15_out,
       xor_16_out, xor_17_out;

  xor xor_1 (OVERFLOW, adder_1_cout, adder_2_cout);
  Adder #(.width(1)) adder_1 (.a(INPUT1[15]), .b(xor_2_out), .out(out_5[15]), .cin(adder_2_cout), .cout(adder_1_cout));
  xor xor_2 (xor_2_out, INPUT2[15], SUB);
  Adder #(.width(1)) adder_2 (.a(INPUT1[14]), .b(xor_3_out), .out(out_5[14]), .cin(adder_3_cout), .cout(adder_2_cout));
  xor xor_3 (xor_3_out, INPUT2[14], SUB);
  Adder #(.width(1)) adder_3 (.a(INPUT1[13]), .b(xor_4_out), .out(out_5[13]), .cin(adder_4_cout), .cout(adder_3_cout));
  xor xor_4 (xor_4_out, INPUT2[13], SUB);
  Adder #(.width(1)) adder_4 (.a(INPUT1[12]), .b(xor_5_out), .out(out_5[12]), .cin(adder_5_cout), .cout(adder_4_cout));
  xor xor_5 (xor_5_out, INPUT2[12], SUB);
  Adder #(.width(1)) adder_5 (.a(INPUT1[11]), .b(xor_6_out), .out(out_5[11]), .cin(adder_6_cout), .cout(adder_5_cout));
  xor xor_6 (xor_6_out, INPUT2[11], SUB);
  Adder #(.width(1)) adder_6 (.a(INPUT1[10]), .b(xor_7_out), .out(out_5[10]), .cin(adder_7_cout), .cout(adder_6_cout));
  xor xor_7 (xor_7_out, INPUT2[10], SUB);
  Adder #(.width(1)) adder_7 (.a(INPUT1[9]), .b(xor_8_out), .out(out_5[9]), .cin(adder_8_cout), .cout(adder_7_cout));
  xor xor_8 (xor_8_out, INPUT2[9], SUB);
  Adder #(.width(1)) adder_8 (.a(INPUT1[8]), .b(xor_9_out), .out(out_5[8]), .cin(adder_9_cout), .cout(adder_8_cout));
  xor xor_9 (xor_9_out, INPUT2[8], SUB);
  Adder #(.width(1)) adder_9 (.a(INPUT1[7]), .b(xor_10_out), .out(out_5[7]), .cin(adder_10_cout), .cout(adder_9_cout));
  xor xor_10 (xor_10_out, INPUT2[7], SUB);
  Adder #(.width(1)) adder_10 (
    .a(INPUT1[6]), .b(xor_11_out), .out(out_5[6]), .cin(adder_11_cout), .cout(adder_10_cout));
  xor xor_11 (xor_11_out, INPUT2[6], SUB);
  Adder #(.width(1)) adder_11 (
    .a(INPUT1[5]), .b(xor_12_out), .out(out_5[5]), .cin(adder_12_cout), .cout(adder_11_cout));
  xor xor_12 (xor_12_out, INPUT2[5], SUB);
  Adder #(.width(1)) adder_12 (
    .a(INPUT1[4]), .b(xor_13_out), .out(out_5[4]), .cin(adder_13_cout), .cout(adder_12_cout));
  xor xor_13 (xor_13_out, INPUT2[4], SUB);
  Adder #(.width(1)) adder_13 (
    .a(INPUT1[3]), .b(xor_14_out), .out(out_5[3]), .cin(adder_14_cout), .cout(adder_13_cout));
  xor xor_14 (xor_14_out, INPUT2[3], SUB);
  Adder #(.width(1)) adder_14 (
    .a(INPUT1[2]), .b(xor_15_out), .out(out_5[2]), .cin(adder_15_cout), .cout(adder_14_cout));
  xor xor_15 (xor_15_out, INPUT2[2], SUB);
  Adder #(.width(1)) adder_15 (
    .a(INPUT1[1]), .b(xor_16_out), .out(out_5[1]), .cin(adder_16_cout), .cout(adder_15_cout));
  xor xor_16 (xor_16_out, INPUT2[1], SUB);
  Adder #(.width(1)) adder_16 (.a(INPUT1[0]), .b(xor_17_out), .out(out_5[0]), .cin(SUB), .cout(adder_16_cout));
  xor xor_17 (xor_17_out, INPUT2[0], SUB);
endmodule

module ALU (
  input  [15:0] INPUT1,
  input  [15:0] INPUT2,
  input  [1:0] SELECTOR,
  output OVERFLOW,
  output [15:0] OUTPUT
);

  wire [15:0] add_sub_1_out_5, AND_out, multiplexer_1_out, OR_out;

  ADD_SUB add_sub_1 (.INPUT1(INPUT1), .OVERFLOW(OVERFLOW), .SUB(SELECTOR[0]), .INPUT2(INPUT2), .out_5(add_sub_1_out_5));
  assign AND_out = INPUT1 & INPUT2;  // AND_Gate AND, 16 bits wide
  assign OR_out = INPUT1 | INPUT2;  // OR_Gate OR, 16 bits wide
  Multiplexer #(.width(16), .enable("false")) multiplexer_1 (
    .in0(AND_out), .in1(OR_out), .out(multiplexer_1_out), .sel(SELECTOR[0]));
  Multiplexer #(.width(16), .enable("false")) multiplexer_2 (
    .in0(add_sub_1_out_5), .in1(multiplexer_1_out), .out(OUTPUT), .sel(SELECTOR[1]));
endmodule

module MEM (
  input  [15:0] ADDRESS,
  input  [15:0] Write_Data,
  input  MemWrite,
  input  Clear,
  input  MemRead,
  output [15:0] OUTPUT
);

  wire Clock_out;

  Clock Clock (.out(Clock_out));
  RAM #(.addrWidth(16), .dataWidth(16), .bus("separate")) ram_1 (
    .addr(ADDRESS), .din(Write_Data), .data(OUTPUT), .str(MemWrite), .sel(1'b1), .clk(Clock_out),
    .ld(MemRead), .clr(Clear));
endmodule

module proje (
  input  Clear,
  input  CLEAR_2,
  input  MemRead,
  output [15:0] ReadData1,
  output [2:0] R_Hedef,
  output OVERFLOW,
  output [2:0] R_Kaynak2,
  output [15:0] OUTPUT,
  output [2:0] R_Kaynak1,
  output [15:0] OUTPUT_2,
  output [1:0] Selector,
  output MemWrite,
  output MemtoReg,
  output [15:0] OUTPUT_3,
  output [15:0] WriteData,
  output [15:0] ReadData2
);

  wire CLOCK_2_out, Clock_3_out, CLOCK_out, decoder_1_out0, decoder_1_out1, decoder_1_out2, decoder_1_out3,
       decoder_1_out4, decoder_1_out5, decoder_1_out6, decoder_1_out7;
  wire [15:0] add_sub_1_out_5, adder_1_out, AND_out, multiplexer_3_out, OR_out, register_1_q, register_2_q,
       register_3_q, register_4_q, register_5_q, register_6_q, register_7_q, register_8_q;
  wire [15:13] rom_1_data;

  Clock CLOCK (.out(CLOCK_out));
  Register #(.width(16)) PC (.D(adder_1_out), .en(1'b1), .Q(OUTPUT_3), .clk(CLOCK_out), .clr(CLEAR_2));
  Adder #(.width(16)) adder_1 (.a(16'h1), .b(OUTPUT_3), .out(adder_1_out));  // open: cin, cout
  ROM #(.addrWidth(16), .dataWidth(16)) rom_1 (
    .addr(OUTPUT_3), .data({rom_1_data, MemtoReg, MemWrite, Selector, R_Kaynak1, R_Kaynak2, R_Hedef}),
    .sel(1'b1));
  Decoder #(.select(3), .enable("false")) decoder_1 (
    .out0(decoder_1_out0), .out1(decoder_1_out1), .out2(decoder_1_out2), .out3(decoder_1_out3),
    .out4(decoder_1_out4), .out5(decoder_1_out5), .out6(decoder_1_out6), .out7(decoder_1_out7), .sel(R_Hedef));
  Register #(.width(16)) register_1 (
    .D(WriteData), .en(decoder_1_out0), .Q(register_1_q), .clk(CLOCK_2_out));  // open: clr
  Register #(.width(16)) register_2 (
    .D(WriteData), .en(decoder_1_out1), .Q(register_2_q), .clk(CLOCK_2_out));  // open: clr
  Register #(.width(16)) register_3 (
    .D(WriteData), .en(decoder_1_out2), .Q(register_3_q), .clk(CLOCK_2_out));  // open: clr
  Register #(.width(16)) register_4 (
    .D(WriteData), .en(decoder_1_out3), .Q(register_4_q), .clk(CLOCK_2_out));  // open: clr
  Register #(.width(16)) register_5 (
    .D(WriteData), .en(decoder_1_out4), .Q(register_5_q), .clk(CLOCK_2_out));  // open: clr
  Register #(.width(16)) register_6 (
    .D(WriteData), .en(decoder_1_out5), .Q(register_6_q), .clk(CLOCK_2_out));  // open: clr
  Register #(.width(16)) register_7 (
    .D(WriteData), .en(decoder_1_out6), .Q(register_7_q), .clk(CLOCK_2_out));  // open: clr
  Register #(.width(16)) register_8 (
    .D(WriteData), .en(decoder_1_out7), .Q(register_8_q), .clk(CLOCK_2_out));  // open: clr
  Clock CLOCK_2 (.out(CLOCK_2_out));
  Multiplexer #(.select(3), .width(16)) multiplexer_1 (
    .in0(register_1_q), .in1(register_2_q), .in2(register_3_q), .in3(register_4_q), .in4(register_5_q),
    .in5(register_6_q), .in6(register_7_q), .in7(register_8_q), .out(ReadData1), .sel(R_Kaynak1));  // open: en
  Multiplexer #(.select(3), .width(16)) multiplexer_2 (
    .in0(register_1_q), .in1(register_2_q), .in2(register_3_q), .in3(register_4_q), .in4(register_5_q),
    .in5(register_6_q), .in6(register_7_q), .in7(register_8_q), .out(ReadData2), .sel(R_Kaynak2));  // open: en
  ADD_SUB add_sub_1 (
    .INPUT1(ReadData1), .OVERFLOW(OVERFLOW), .SUB(Selector[0]), .INPUT2(ReadData2), .out_5(add_sub_1_out_5));
  assign AND_out = ReadData1 & ReadData2;  // AND_Gate AND, 16 bits wide
  assign OR_out = ReadData1 | ReadData2;  // OR_Gate OR, 16 bits wide
  Multiplexer #(.width(16), .enable("false")) multiplexer_3 (
    .in0(AND_out), .in1(OR_out), .out(multiplexer_3_out), .sel(Selector[0]));
  Multiplexer #(.width(16), .enable("false")) multiplexer_4 (
    .in0(add_sub_1_out_5), .in1(multiplexer_3_out), .out(OUTPUT_2), .sel(Selector[1]));
  Clock Clock_3 (.out(Clock_3_out));
  RAM #(.addrWidth(16), .dataWidth(16), .bus("separate")) ram_1 (
    .addr(OUTPUT_2), .din(ReadData2), .data(OUTPUT), .str(MemWrite), .sel(1'b1), .clk(Clock_3_out),
    .ld(MemRead), .clr(Clear));
  Multiplexer #(.width(16), .enable("false")) multiplexer_5 (
    .in0(OUTPUT_2), .in1(OUTPUT), .out(WriteData), .sel(MemtoReg));

  // Notes on the sheet:
  //   sub r3 r2 r1 -->000 0 0 01 001 010 011 --> 0253
  //   str r0, r6 -->000 0 1 00 000 110 000 --> 0830 
  //   contents of rom_1 (hex, n*v repeats v):
  //   253 830
endmodule
